// Logisim project control-logic.circ as structural Verilog: 1 circuit, main circuit control_logic
module control_logic (
  input  [31:0] Instruction,
  input  BrEq,
  input  BrLt,
  output PCSel,
  output RegWEn,
  output [2:0] ImmSel,
  output BrUn,
  output ASel,
  output BSel,
  output [3:0] ALUSel,
  output MemWEn,
  output [1:0] WBSel
);

  wire comparator_3_eq, comparator_4_eq, comparator_5_eq, comparator_6_eq, comparator_7_eq, comparator_8_eq,
       comparator_9_eq, comparator_10_eq, comparator_11_eq, comparator_12_eq, comparator_13_eq,
       comparator_15_eq, comparator_16_eq, comparator_17_eq, comparator_18_eq, comparator_19_eq,
       comparator_20_eq, comparator_21_eq, comparator_22_eq, comparator_23_eq, comparator_24_eq,
       comparator_25_eq, comparator_26_eq, comparator_27_eq, comparator_28_eq, comparator_29_eq,
       comparator_30_eq, comparator_31_eq, comparator_32_eq, comparator_33_eq, comparator_34_eq,
       comparator_35_eq, comparator_36_eq, comparator_37_eq, comparator_38_eq, comparator_40_eq,
       comparator_41_eq, comparator_42_eq, comparator_43_eq, comparator_44_eq, comparator_45_eq, is_add,
       is_addi, is_and, is_andi, is_B, is_beq, is_bge, is_bgeu, is_blt, is_bltu, is_bne, is_I, is_mul,
       is_mulh, is_mulhu, is_or, is_ori, is_R, is_sll, is_slli, is_slt, is_slti, is_sra, is_srai, is_srl,
       is_srli, is_sub, is_xor, is_xori;
  wire [5:0] priority_encoder_1_p19;
  wire [15:14] rom_1_data;

  ROM #(.addrWidth(6), .dataWidth(16)) rom_1 (
    .addr(priority_encoder_1_p19),
    .data({rom_1_data, WBSel, MemWEn, ALUSel, BSel, ASel, BrUn, ImmSel, RegWEn}));
  // Priority_Encoder #(.select_enc(6)) priority_encoder_1: pin names not known; wires that end beside it: is_xor, is_srl, is_sra, is_or, is_and, is_addi, is_slli, is_slti, is_xori, is_srli, is_srai, is_ori, is_andi, is_beq, is_bne, is_blt, is_bge, is_bltu, priority_encoder_1_p19, is_bgeu
  Comparator #(.mode("unsigned"), .width(7)) comparator_1 (
    .a(Instruction[6:0]), .b(7'b0010011), .eq(is_I));  // open: gt, lt
  Comparator comparator_2 ();  // open: a, b, gt, eq, lt
  Comparator #(.mode("unsigned"), .width(7)) comparator_3 (
    .a(Instruction[31:25]), .b({7{1'b0}}), .eq(comparator_3_eq));  // open: gt, lt
  Comparator #(.mode("unsigned"), .width(3)) comparator_4 (
    .a(Instruction[14:12]), .b(3'b101), .eq(comparator_4_eq));  // open: gt, lt
  Comparator #(.mode("unsigned"), .width(7)) comparator_5 (
    .a(Instruction[31:25]), .b(7'b0100000), .eq(comparator_5_eq));  // open: gt, lt
  Comparator #(.mode("unsigned"), .width(3)) comparator_6 (
    .a(Instruction[14:12]), .b(3'b101), .eq(comparator_6_eq));  // open: gt, lt
  Comparator #(.mode("unsigned"), .width(7)) comparator_7 (
    .a(Instruction[31:25]), .b({7{1'b0}}), .eq(comparator_7_eq));  // open: gt, lt
  Comparator #(.mode("unsigned"), .width(3)) comparator_8 (
    .a(Instruction[14:12]), .b(3'b001), .eq(comparator_8_eq));  // open: gt, lt
  Comparator #(.mode("unsigned"), .width(3)) comparator_9 (
    .a(Instruction[14:12]), .b(3'b000), .eq(comparator_9_eq));  // open: gt, lt
  Comparator #(.mode("unsigned"), .width(3)) comparator_10 (
    .a(Instruction[14:12]), .b(3'b111), .eq(comparator_10_eq));  // open: gt, lt
  Comparator #(.mode("unsigned"), .width(3)) comparator_11 (
    .a(Instruction[14:12]), .b(3'b110), .eq(comparator_11_eq));  // open: gt, lt
  Comparator #(.mode("unsigned"), .width(3)) comparator_12 (
    .a(Instruction[14:12]), .b(3'b100), .eq(comparator_12_eq));  // open: gt, lt
  Comparator #(.mode("unsigned"), .width(3)) comparator_13 (
    .a(Instruction[14:12]), .b(3'b010), .eq(comparator_13_eq));  // open: gt, lt
  and and_1 (is_addi, comparator_9_eq, is_I);
  and and_2 (is_andi, comparator_10_eq, is_I);
  and and_3 (is_ori, comparator_11_eq, is_I);
  and and_4 (is_xori, comparator_12_eq, is_I);
  and and_5 (is_slti, comparator_13_eq, is_I);
  and and_6 (is_srli, is_I, comparator_3_eq, comparator_4_eq);
  and and_7 (is_srai, is_I, comparator_5_eq, comparator_6_eq);
  and and_8 (is_slli, is_I, comparator_7_eq, comparator_8_eq);
  Comparator #(.mode("unsigned"), .width(7)) comparator_14 (
    .a(Instruction[6:0]), .b(7'b0110011), .eq(is_R));  // open: gt, lt
  Comparator #(.mode("unsigned"), .width(7)) comparator_15 (
    .a(Instruction[31:25]), .b({7{1'b0}}), .eq(comparator_15_eq));  // open: gt, lt
  Comparator #(.mode("unsigned"), .width(3)) comparator_16 (
    .a(Instruction[14:12]), .b(3'b000), .eq(comparator_16_eq));  // open: gt, lt
  Comparator #(.mode("unsigned"), .width(7)) comparator_17 (
    .a(Instruction[31:25]), .b(7'b0100000), .eq(comparator_17_eq));  // open: gt, lt
  Comparator #(.mode("unsigned"), .width(3)) comparator_18 (
    .a(Instruction[14:12]), .b(3'b000), .eq(comparator_18_eq));  // open: gt, lt
  Comparator #(.mode("unsigned"), .width(7)) comparator_19 (
    .a(Instruction[31:25]), .b({7{1'b0}}), .eq(comparator_19_eq));  // open: gt, lt
  Comparator #(.mode("unsigned"), .width(3)) comparator_20 (
    .a(Instruction[14:12]), .b(3'b111), .eq(comparator_20_eq));  // open: gt, lt
  Comparator #(.mode("unsigned"), .width(7)) comparator_21 (
    .a(Instruction[31:25]), .b({7{1'b0}}), .eq(comparator_21_eq));  // open: gt, lt
  Comparator #(.mode("unsigned"), .width(3)) comparator_22 (
    .a(Instruction[14:12]), .b(3'b110), .eq(comparator_22_eq));  // open: gt, lt
  Comparator #(.mode("unsigned"), .width(7)) comparator_23 (
    .a(Instruction[31:25]), .b({7{1'b0}}), .eq(comparator_23_eq));  // open: gt, lt
  Comparator #(.mode("unsigned"), .width(3)) comparator_24 (
    .a(Instruction[14:12]), .b(3'b100), .eq(comparator_24_eq));  // open: gt, lt
  Comparator #(.mode("unsigned"), .width(7)) comparator_25 (
    .a(Instruction[31:25]), .b({7{1'b0}}), .eq(comparator_25_eq));  // open: gt, lt
  Comparator #(.mode("unsigned"), .width(3)) comparator_26 (
    .a(Instruction[14:12]), .b(3'b001), .eq(comparator_26_eq));  // open: gt, lt
  Comparator #(.mode("unsigned"), .width(7)) comparator_27 (
    .a(Instruction[31:25]), .b({7{1'b0}}), .eq(comparator_27_eq));  // open: gt, lt
  Comparator #(.mode("unsigned"), .width(3)) comparator_28 (
    .a(Instruction[14:12]), .b(3'b101), .eq(comparator_28_eq));  // open: gt, lt
  Comparator #(.mode("unsigned"), .width(7)) comparator_29 (
    .a(Instruction[31:25]), .b(7'b0100000), .eq(comparator_29_eq));  // open: gt, lt
  Comparator #(.mode("unsigned"), .width(3)) comparator_30 (
    .a(Instruction[14:12]), .b(3'b101), .eq(comparator_30_eq));  // open: gt, lt
  Comparator #(.mode("unsigned"), .width(7)) comparator_31 (
    .a(Instruction[31:25]), .b({7{1'b0}}), .eq(comparator_31_eq));  // open: gt, lt
  Comparator #(.mode("unsigned"), .width(3)) comparator_32 (
    .a(Instruction[14:12]), .b(3'b010), .eq(comparator_32_eq));  // open: gt, lt
  Comparator #(.mode("unsigned"), .width(7)) comparator_33 (
    .a(Instruction[31:25]), .b(7'b0000001), .eq(comparator_33_eq));  // open: gt, lt
  Comparator #(.mode("unsigned"), .width(3)) comparator_34 (
    .a(Instruction[14:12]), .b(3'b000), .eq(comparator_34_eq));  // open: gt, lt
  Comparator #(.mode("unsigned"), .width(7)) comparator_35 (
    .a(Instruction[31:25]), .b(7'b0000001), .eq(comparator_35_eq));  // open: gt, lt
  Comparator #(.mode("unsigned"), .width(3)) comparator_36 (
    .a(Instruction[14:12]), .b(3'b001), .eq(comparator_36_eq));  // open: gt, lt
  Comparator #(.mode("unsigned"), .width(7)) comparator_37 (
    .a(Instruction[31:25]), .b(7'b0000001), .eq(comparator_37_eq));  // open: gt, lt
  Comparator #(.mode("unsigned"), .width(3)) comparator_38 (
    .a(Instruction[14:12]), .b(3'b011), .eq(comparator_38_eq));  // open: gt, lt
  and and_9 (is_add, is_R, comparator_15_eq, comparator_16_eq);
  and and_10 (is_sub, is_R, comparator_17_eq, comparator_18_eq);
  and and_11 (is_and, is_R, comparator_19_eq, comparator_20_eq);
  and and_12 (is_or, is_R, comparator_21_eq, comparator_22_eq);
  and and_13 (is_xor, is_R, comparator_23_eq, comparator_24_eq);
  and and_14 (is_sll, is_R, comparator_25_eq, comparator_26_eq);
  and and_15 (is_srl, is_R, comparator_27_eq, comparator_28_eq);
  and and_16 (is_sra, is_R, comparator_29_eq, comparator_30_eq);
  and and_17 (is_slt, is_R, comparator_31_eq, comparator_32_eq);
  and and_18 (is_mul, is_R, comparator_33_eq, comparator_34_eq);
  and and_19 (is_mulh, is_R, comparator_35_eq, comparator_36_eq);
  and and_20 (is_mulhu, is_R, comparator_37_eq, comparator_38_eq);
  Comparator #(.mode("unsigned"), .width(7)) comparator_39 (
    .a(Instruction[6:0]), .b(7'b1100011), .eq(is_B));  // open: gt, lt
  Comparator #(.mode("unsigned"), .width(3)) comparator_40 (
    .a(Instruction[14:12]), .b(3'b000), .eq(comparator_40_eq));  // open: gt, lt
  Comparator #(.mode("unsigned"), .width(3)) comparator_41 (
    .a(Instruction[14:12]), .b(3'b101), .eq(comparator_41_eq));  // open: gt, lt
  Comparator #(.mode("unsigned"), .width(3)) comparator_42 (
    .a(Instruction[14:12]), .b(3'b111), .eq(comparator_42_eq));  // open: gt, lt
  Comparator #(.mode("unsigned"), .width(3)) comparator_43 (
    .a(Instruction[14:12]), .b(3'b100), .eq(comparator_43_eq));  // open: gt, lt
  Comparator #(.mode("unsigned"), .width(3)) comparator_44 (
    .a(Instruction[14:12]), .b(3'b110), .eq(comparator_44_eq));  // open: gt, lt
  Comparator #(.mode("unsigned"), .width(3)) comparator_45 (
    .a(Instruction[14:12]), .b(3'b001), .eq(comparator_45_eq));  // open: gt, lt
  and and_21 (is_beq, comparator_40_eq, is_B);
  and and_22 (is_bge, comparator_41_eq, is_B);
  and and_23 (is_bgeu, comparator_42_eq, is_B);
  and and_24 (is_blt, comparator_43_eq, is_B);
  and and_25 (is_bltu, comparator_44_eq, is_B);
  and and_26 (is_bne, comparator_45_eq, is_B);

  // Other names for the same wires on the sheet: opcode[6:0] = Instruction[6:0]; fun3[2:0] = Instruction[14:12];
  //   fun7[6:0] = Instruction[31:25]

  // Notes on the sheet:
  //   INPUTS to your circuit
  //   Connect ROM Input here ->
  //   contents of rom_1 (hex, n*v repeats v):
  //   1061 1461 1661 10e1 14e1 15e1 1161 1261 12e1 16e1 1361 13e1 0 0 0 1021 10a1 1121 1221 12a1 16a1 1321
  //   13a1
  //   ROM FOR CONTROL LOGIC
  //   DON'T CHANGE THE LOCATIONS OF THE INPUTS AND OUTPUTS!
  //   This is only if you choose to do the ROM option
  //   OUTPUT from your circuit
  //   Reminder: If using ROM, use combinational logic for PCSel
endmodule
