// Logisim project partial-store.circ as structural Verilog: 1 circuit, main circuit partial_store
module partial_store (
  input  [31:0] Instruction,
  input  [31:0] MemAddress,
  input  [31:0] DataFromReg,
  input  MemWEn,
  output [3:0] MemWriteMask,
  output [31:0] DataToMem
);

  wire [1:0] multiplexer_3_out;
  wire [3:0] shifter_4_out, shifter_5_out;
  wire [4:0] bit_extender_1_out, shifter_1_out;
  wire [31:0] bit_extender_2_out, bit_extender_3_out, shifter_2_out, shifter_3_out;

  assign bit_extender_1_out = {{3{1'b0}}, MemAddress[1:0]};  // Bit_Extender bit_extender_1
  Shifter #(.width(5)) shifter_1 (.in(bit_extender_1_out), .\dist (3'b011), .out(shifter_1_out));
  assign bit_extender_2_out = {{16{1'b0}}, DataFromReg[15:0]};  // Bit_Extender bit_extender_2
  assign bit_extender_3_out = {{24{1'b0}}, DataFromReg[7:0]};  // Bit_Extender bit_extender_3
  Shifter #(.width(32)) shifter_2 (.in(bit_extender_2_out), .\dist (shifter_1_out), .out(shifter_2_out));
  Shifter #(.width(32)) shifter_3 (.in(bit_extender_3_out), .\dist (shifter_1_out), .out(shifter_3_out));
  Shifter #(.width(4)) shifter_4 (.in(4'b0011), .\dist (MemAddress[1:0]), .out(shifter_4_out));
  Shifter #(.width(4)) shifter_5 (.in(4'b0001), .\dist (MemAddress[1:0]), .out(shifter_5_out));
  Multiplexer #(.select(2), .width(32)) multiplexer_1 (
    .in0(shifter_3_out), .in1(shifter_2_out), .in2(DataFromReg), .out(DataToMem), .sel(Instruction[13:12]));  // open: in3
  Multiplexer #(.select(2), .width(4)) multiplexer_2 (
    .in0(shifter_5_out), .in1(shifter_4_out), .in2(4'b1111), .in3(4'b0000), .out(MemWriteMask),
    .sel(multiplexer_3_out));
  Multiplexer #(.width(2)) multiplexer_3 (.in0(2'b11), .in1(Instruction[13:12]), .out(multiplexer_3_out), .sel(MemWEn));

  // Notes on the sheet:
  //   INPUTS to your circuit
  //   DON'T CHANGE THE LOCATIONS OF THE INPUTS AND OUTPUTS!
  //   OUTPUT from your circuit
endmodule
