// Logisim project ex2.circ as structural Verilog: 1 circuit, main circuit compute_BrUn
module compute_BrUn (
  input  [31:0] INSTRUCTION,
  output BrUn
);

  wire comparator_1_lt;

  Comparator #(.mode("unsigned"), .width(3)) comparator_1 (
    .a(INSTRUCTION[14:12]), .b(3'b110), .lt(comparator_1_lt));  // open: gt, eq
  Multiplexer multiplexer_1 (.in0(1'b1), .in1(1'b0), .out(BrUn), .sel(comparator_1_lt));
endmodule
